// Digital circuit instruction_memory.dig as structural Verilog
module instruction_memory (
  input  [31:0] A,
  input  [3:0] PN,
  output [31:0] D
);

  wire [31:0] foo_2_d, foo_3_d, foo_d;

  ROM #(.AddrBits(6), .Bits(32)) foo (.A(A[5:0]), .sel(1'b1), .D(foo_d));
  ROM #(.AddrBits(6), .Bits(32)) foo_2 (.A(A[5:0]), .sel(1'b1), .D(foo_2_d));
  ROM #(.AddrBits(6), .Bits(32)) foo_3 (.A(A[5:0]), .sel(1'b1), .D(foo_3_d));
  Multiplexer #(.Selector_Bits(4), .Bits(32)) multiplexer_1 (
    .sel(PN), .in_0(foo_d), .in_1(foo_2_d), .in_2(foo_3_d), .in_3({32{1'b0}}), .in_4({32{1'b0}}),
    .in_5({32{1'b0}}), .in_6({32{1'b0}}), .in_7({32{1'b0}}), .in_8({32{1'b0}}), .in_9({32{1'b0}}),
    .in_10({32{1'b0}}), .in_11({32{1'b0}}), .in_12({32{1'b0}}), .in_13({32{1'b0}}), .in_14({32{1'b0}}),
    .in_15({32{1'b0}}), .out(D));
  // Pins of 6 and 32 bits meet at A
endmodule
