// Digital circuit embedded_test.dig as structural Verilog
module embedded_test (
  input  in_1,
  input  in_2,
  output out_3
);

  // Probe on in_1
  and_subcircuit and_subcircuit_1 (.A(in_1), .B(in_2), .OUT(out_3));
  // Probe on in_2
  // Probe on out_3
endmodule
