// Digital circuit gate_test.dig as structural Verilog
module gate_test (
  input  A,
  input  B,
  output A_AND_B,
  output A_OR_B,
  output NOT_A,
  output NOT_B
);

  // Probe on A
  // Probe on B
  and and_1 (A_AND_B, A, B);
  or or_1 (A_OR_B, A, B);
  not not_1 (NOT_A, A);
  not not_2 (NOT_B, B);
  // Probe on A_AND_B
  // Probe on A_OR_B
  // Probe on NOT_A
  // Probe on NOT_B
  LED led_1 (.in(A_AND_B));
  LED led_2 (.in(A_OR_B));
  LED led_3 (.in(NOT_A));
  LED led_4 (.in(NOT_B));
endmodule
