// Digital circuit half_adder.dig as structural Verilog
module half_adder (
  input  A,
  input  B,
  output Cout,
  output Sum
);

  wire and_1_out, and_2_out, not_1_out, not_2_out;

  not not_1 (not_1_out, A);
  not not_2 (not_2_out, B);
  and and_1 (and_1_out, not_1_out, B);
  and and_2 (and_2_out, A, not_2_out);
  and and_3 (Cout, A, B);
  or or_1 (Sum, and_1_out, and_2_out);
endmodule
