// Digital circuit half_adder_main.dig as structural Verilog
module half_adder_main (
  input  A,
  input  B,
  output Sum,
  output Cout
);

  half_adder Half_Adder (.A(A), .B(B), .Cout(Sum), .Sum(Cout));
endmodule
