// Digital circuit test_graphics_ram.dig as structural Verilog
module test_graphics_ram (
  input  [6:0] Pixel,
  input  [6:0] ADDR,
  input  STR,
  input  CLK,
  input  LD,
  input  Buffer
);

  GraphicCard #(.Bits(7), .graphicHeight(8), .graphicWidth(8)) Display (
    .A(ADDR), .str(STR), .C(CLK), .ld(LD), .B(Buffer), .D(Pixel));
endmodule
