// Digital circuit test_image_rom.dig as structural Verilog
module test_image_rom (
  input  [2:0] Row,
  input  [2:0] BitSel,
  output [7:0] out_1,
  output out_4
);

  ROM #(.AddrBits(3), .Bits(8)) Images (.A(Row), .sel(1'b1), .D(out_1));
  Multiplexer #(.Selector_Bits(3)) multiplexer_1 (
    .sel(BitSel), .in_0(out_1[0]), .in_1(out_1[1]), .in_2(out_1[2]), .in_3(out_1[3]), .in_4(out_1[4]),
    .in_5(out_1[5]), .in_6(out_1[6]), .in_7(out_1[7]), .out(out_4));
  // Probe on out_4

  // Notes on the sheet:
  //   contents of Images (hex, n*v repeats v):
  //   7e,42,42,42,42,7e,18,18
endmodule
