// Digital circuit test_rom.dig as structural Verilog
module test_rom (
  input  [15:0] in_2,
  input  in_3,
  input  clk,
  output [15:0] out_1
);

  Register #(.Bits(16)) Reg16 (.D(in_2), .C(clk), .en(in_3), .Q(out_1));
endmodule
